// Logisim project MiniCounter.circ as structural Verilog: 20 circuits, main circuit 数码管驱动
// LED计数
module \LED计数电路  (
);


  // Notes on the sheet:
  //   此电路空白，需要你从头绘制！
endmodule

module \LED计数测试  (
);


  // Notes on the sheet:
  //   此电路空白，需要你从头绘制！
endmodule

// 编码器
module \_5输入编码器  (
);


  // Notes on the sheet:
  //   此电路空白，需要你从头绘制！
endmodule

module \数码管驱动  (
  input  X3,
  input  X2,
  input  X1,
  input  X0,
  output Seg_1,
  output Seg_2,
  output Seg_3,
  output Seg_4,
  output Seg_5,
  output Seg_6,
  output Seg_7
);
endmodule

module \数码管驱动测试  (
);

  wire clock_1_out, \数码管驱动_1_seg_1 , \数码管驱动_1_seg_2 , \数码管驱动_1_seg_3 , \数码管驱动_1_seg_4 , \数码管驱动_1_seg_5 ,
       \数码管驱动_1_seg_6 , \数码管驱动_1_seg_7 ;
  wire [3:0] counter_1_q;

  Counter #(.width(4), .max('hf), .ongoal("wrap"), .trigger("rising"), .behavior("old")) counter_1 (
    .Q(counter_1_q), .clk(clock_1_out));  // open: load, D, count, carry, clr, preset
  Clock #(.highDuration(1), .lowDuration(1)) clock_1 (.out(clock_1_out));
  \数码管驱动  \u_数码管驱动_1  (
    .X3(counter_1_q[3]), .Seg_1(\数码管驱动_1_seg_1 ), .X2(counter_1_q[2]), .Seg_2(\数码管驱动_1_seg_2 ),
    .X1(counter_1_q[1]), .Seg_3(\数码管驱动_1_seg_3 ), .X0(counter_1_q[0]), .Seg_4(\数码管驱动_1_seg_4 ),
    .Seg_5(\数码管驱动_1_seg_5 ), .Seg_6(\数码管驱动_1_seg_6 ), .Seg_7(\数码管驱动_1_seg_7 ));
  _7_Segment_Display #(.active("true")) u_7_segment_display_1 (
    .g(\数码管驱动_1_seg_1 ), .f(\数码管驱动_1_seg_2 ), .a(\数码管驱动_1_seg_3 ), .b(\数码管驱动_1_seg_4 ), .e(\数码管驱动_1_seg_5 ),
    .d(\数码管驱动_1_seg_6 ), .c(\数码管驱动_1_seg_7 ));  // open: dp

  // Notes on the sheet:
  //   Ctrl+T驱动时钟单步运行测试
endmodule

// 4位数比较器
module \_4位无符号比较器  (
  input  X3,
  input  X2,
  input  X1,
  input  X0,
  input  Y3,
  input  Y2,
  input  Y1,
  input  Y0,
  output Great,
  output Equal,
  output Less
);
endmodule

module \_8位无符号比较器  (
  input  [7:0] X,
  input  [7:0] Y,
  output Great,
  output Equal,
  output Less
);

  // Probe on X
  // Probe on Y
  \_4位无符号比较器  \u_4位无符号比较器_1  ();  // open: X3, X2, X1, X0, Y3, Y2, Y1, Y0, Great, Equal, Less
  \_4位无符号比较器  \u_4位无符号比较器_2  ();  // open: X3, X2, X1, X0, Y3, Y2, Y1, Y0, Great, Equal, Less

  // Other names for the same wires on the sheet: X0[3:0] = X[3:0]; X1[3:0] = X[7:4]; Y0[3:0] = Y[3:0];
  //   Y1[3:0] = Y[7:4]

  // Notes on the sheet:
  //   请勿增删改引脚，否则可能导致电路封装变化，无法测试
  //   请勿增删改引脚，请在下方利用上方输入输出引脚的隧道标签信号构建电路，ctrl+d复制选择组件
  //   电路功能：X,Y进行无符号比较，Great=(X>Y)?1:0;
  //   输出引脚区
endmodule

// MUX
module \_2路选择器_1位  (
  input  X0,
  input  Sel,
  input  X1,
  output Out
);


  // Notes on the sheet:
  //   请勿增删改引脚，否则可能导致电路封装变化，无法测试
  //   请勿增删改引脚，请在下方利用上方输入输出引脚的隧道标签信号构建电路，ctrl+d复制选择组件
  //   输入引脚区
  //   输出引脚区
  //   电路功能：Out=(Sel==0)?X0:X1;
endmodule

// MUX
module \_2路选择器_4位  (
  input  [3:0] X,
  input  Sel,
  input  [3:0] Y,
  output [3:0] Out
);

  // Probe on X
  // Probe on Y
  // Probe on Out

  // Notes on the sheet:
  //   请勿增删改引脚，否则可能导致电路封装变化，无法测试！
  //   请勿增删改引脚，请在下方利用上方输入输出引脚的隧道标签信号构建电路，ctrl+d复制选择组件
  //   输入引脚区
  //   电路功能：Out=(Sel==0)?X:Y;
  //   输出引脚区
endmodule

// BCD计数
module \BCD双向计数器_可异步置位  (
  input  CLK,
  input  \使能 ,
  input  \异步置位 ,
  input  [3:0] \预置数据 ,
  input  \计数模式 ,
  input  \复位 ,
  output [3:0] \输出Q ,
  output \进位_借位 
);

  wire D0, D1, D2, D3, or_1_out, undriven;
  wire [3:0] \n2路选择器_4位_1_out ;

  Pull_Resistor #(.pull(0)) pull_resistor_1 (.node(\异步置位 ));
  Pull_Resistor #(.pull(0)) pull_resistor_2 (.node(\计数模式 ));
  \BCD双向计数器状态转换_自动生成  \bcd双向计数器状态转换_自动生成_1  ();  // open: S3, N3, S2, N2, S1, N1, S0, N0, Mode
  \BCD双向计数器输出函数_自动生成  \bcd双向计数器输出函数_自动生成_1  (.Cout(\进位_借位 ));  // open: S3, S2, S1, S0, Mode
  Pull_Resistor #(.pull(1)) pull_resistor_3 (.node(\使能 ));
  Pull_Resistor #(.pull(0)) pull_resistor_4 (.node(\预置数据 ));
  Pull_Resistor #(.pull(0)) pull_resistor_5 (.node(\复位 ));
  \_2路选择器_4位  \u_2路选择器_4位_1  (.X(\预置数据 ), .Out(\n2路选择器_4位_1_out ), .Sel(\复位 ), .Y(4'b0000));
  D_Flip_Flop #(.trigger("rising"), .Pre_Clr_Positions("LEGACY"), .NegatePresetClear("false"), .enable("true"), .NewFFLayout("false")) u_D3 ();  // open: clk, D, Q, Qn, preset, en, reset
  D_Flip_Flop #(.trigger("rising"), .Pre_Clr_Positions("LEGACY"), .NegatePresetClear("false"), .enable("true"), .NewFFLayout("false")) u_D2 ();  // open: clk, D, Q, Qn, preset, en, reset
  D_Flip_Flop #(.trigger("rising"), .Pre_Clr_Positions("LEGACY"), .NegatePresetClear("false"), .enable("true"), .NewFFLayout("false")) u_D1 (.reset(undriven));  // open: clk, D, Q, Qn, preset, en
  D_Flip_Flop #(.trigger("rising"), .Pre_Clr_Positions("LEGACY"), .NegatePresetClear("false"), .enable("true"), .NewFFLayout("false")) u_D0 ();  // open: clk, D, Q, Qn, preset, en, reset
  assign {D3, D2, D1, D0} = or_1_out ? \n2路选择器_4位_1_out  : 4'bz;  // Controlled_Buffer controlled_buffer_1
  or or_1 (or_1_out, \复位 , \异步置位 );
  // Probe on \输出Q 

  // Other names for the same wires on the sheet: Cout = \进位_借位 ; Din[3:0] = \预置数据 ; En = \使能 ; Mode = \计数模式 ;
  //   PreSet = \异步置位 ; Q[3:0] = \输出Q ; RST = \复位 

  // Notes on the sheet:
  //   请勿增删改引脚，否则可能导致电路封装变化，无法测试！！！
  //   上拉下拉电阻用于给出引脚悬空的时的默认值
  //   D3D2D1D0分别接D触发器异步置位和复位端实现异步置位
  //   正计数到9，倒计数到0时输出为1
endmodule

// 状态转换
module \BCD双向计数器状态转换_自动生成  (
  input  S3,
  input  S2,
  input  S1,
  input  S0,
  input  Mode,
  output N3,
  output N2,
  output N1,
  output N0
);
endmodule

module \BCD双向计数器输出函数_自动生成  (
  input  S3,
  input  S2,
  input  S1,
  input  S0,
  input  Mode,
  output Cout
);
endmodule

// 0~5计数
module \_0_5双向计数器_可异步置位  (
  input  CLK,
  input  \使能 ,
  input  \异步置位 ,
  input  [3:0] \预置数据 ,
  input  \计数模式 ,
  input  RST,
  output [3:0] \输出Q ,
  output \进位_借位 
);

  wire D0, D1, D2, D3, or_1_out;
  wire [3:0] \n2路选择器_4位_1_out ;

  Pull_Resistor #(.pull(0)) pull_resistor_1 (.node(\异步置位 ));
  Pull_Resistor #(.pull(0)) pull_resistor_2 (.node(\计数模式 ));
  \_0_5双向计数器输出函数_自动生成  \u_0_5双向计数器输出函数_自动生成_1  ();  // open: S3, Cout, S2, S1, S0, Mode
  \_0_5双向计数器状态转换_自动生成  \u_0_5双向计数器状态转换_自动生成_1  ();  // open: S3, N3, S2, N2, S1, N1, S0, N0, Mode
  Pull_Resistor #(.pull(1)) pull_resistor_3 (.node(\使能 ));
  Pull_Resistor #(.pull(0)) pull_resistor_4 (.node(\预置数据 ));
  Pull_Resistor #(.pull(0)) pull_resistor_5 (.node(RST));
  D_Flip_Flop #(.trigger("rising"), .Pre_Clr_Positions("LEGACY"), .NegatePresetClear("false"), .enable("true"), .NewFFLayout("false")) u_D3 ();  // open: clk, D, Q, Qn, preset, en, reset
  D_Flip_Flop #(.trigger("rising"), .Pre_Clr_Positions("LEGACY"), .NegatePresetClear("false"), .enable("true"), .NewFFLayout("false")) u_D2 ();  // open: clk, D, Q, Qn, preset, en, reset
  D_Flip_Flop #(.trigger("rising"), .Pre_Clr_Positions("LEGACY"), .NegatePresetClear("false"), .enable("true"), .NewFFLayout("false")) u_D1 ();  // open: clk, D, Q, Qn, preset, en, reset
  D_Flip_Flop #(.trigger("rising"), .Pre_Clr_Positions("LEGACY"), .NegatePresetClear("false"), .enable("true"), .NewFFLayout("false")) u_D0 ();  // open: clk, D, Q, Qn, preset, en, reset
  \_2路选择器_4位  \u_2路选择器_4位_1  (.X(\预置数据 ), .Out(\n2路选择器_4位_1_out ), .Sel(RST), .Y(4'b0000));
  assign {D3, D2, D1, D0} = or_1_out ? \n2路选择器_4位_1_out  : 4'bz;  // Controlled_Buffer controlled_buffer_1
  or or_1 (or_1_out, RST, \异步置位 );
  // Probe on \输出Q 

  // Other names for the same wires on the sheet: Cout = \进位_借位 ; Din[3:0] = \预置数据 ; En = \使能 ; Mode = \计数模式 ;
  //   PreSet = \异步置位 ; Q[3:0] = \输出Q 

  // Notes on the sheet:
  //   请勿增删改引脚，否则可能导致电路封装变化，无法测试！！！
  //   上拉下拉电阻用于给出引脚悬空的时的默认值
  //   D3D2D1D0分别接D触发器异步置位和复位端实现异步置位
  //   正计数到9，倒计数到0时输出为1
endmodule

// 状态转换
module \_0_5双向计数器状态转换_自动生成  (
  input  S3,
  input  S2,
  input  S1,
  input  S0,
  input  Mode,
  output N3,
  output N2,
  output N1,
  output N0
);
endmodule

module \_0_5双向计数器输出函数_自动生成  (
  input  S3,
  input  S2,
  input  S1,
  input  S0,
  input  Mode,
  output Cout
);
endmodule

// 0~59双向计数
module \_0_59双向计数器  (
  input  CLK,
  input  \使能 ,
  input  \异步置位 ,
  input  [7:0] \预置数据 ,
  input  \计数模式 ,
  input  RST,
  output [7:0] \输出Q ,
  output \进位_借位 
);

  Pull_Resistor #(.pull(0)) pull_resistor_1 (.node(\异步置位 ));
  Pull_Resistor #(.pull(0)) pull_resistor_2 (.node(\计数模式 ));
  \_0_5双向计数器_可异步置位  \u_0_5双向计数器_可异步置位_1  ();  // open: CLK, 使能, 异步置位, 预置数据, 计数模式, 输出Q, 进位_借位, RST
  Pull_Resistor #(.pull(1)) pull_resistor_3 (.node(\使能 ));
  Pull_Resistor #(.pull(0)) pull_resistor_4 (.node(\预置数据 ));
  Pull_Resistor #(.pull(0)) pull_resistor_5 (.node(RST));
  \BCD双向计数器_可异步置位  \bcd双向计数器_可异步置位_1  ();  // open: CLK, 使能, 输出Q, 异步置位, 预置数据, 进位_借位, 计数模式, 复位

  // Other names for the same wires on the sheet: Cout = \进位_借位 ; Din[7:0] = \预置数据 ; Din0[3:0] = \预置数据 [3:0];
  //   Din1[3:0] = \预置数据 [7:4]; En = \使能 ; Mode = \计数模式 ; PreSet = \异步置位 ; Q[7:0] = \输出Q 

  // Notes on the sheet:
  //   请勿增删改引脚，否则可能导致电路封装变化，无法测试！！！
  //   正计数到59，倒计数到0时输出为1
endmodule

// 倒计数
module \_59分59秒双向计数器  (
  input  CLK,
  input  \使能 ,
  input  \异步置位 ,
  input  [15:0] \预置数据 ,
  input  \计数模式 ,
  input  RST,
  output [7:0] Minute,
  output [7:0] Second,
  output \进位_借位 
);

  Pull_Resistor #(.pull(0)) pull_resistor_1 (.node(\异步置位 ));
  Pull_Resistor #(.pull(0)) pull_resistor_2 (.node(\计数模式 ));
  \_0_59双向计数器  \u_0_59双向计数器_1  ();  // open: CLK, 使能, 输出Q, 异步置位, 预置数据, 进位_借位, 计数模式, RST
  Pull_Resistor #(.pull(1)) pull_resistor_3 (.node(\使能 ));
  Pull_Resistor #(.pull(0)) pull_resistor_4 (.node(\预置数据 ));
  Pull_Resistor #(.pull(0)) pull_resistor_5 (.node(RST));
  \_0_59双向计数器  \u_0_59双向计数器_2  ();  // open: CLK, 使能, 输出Q, 异步置位, 预置数据, 进位_借位, 计数模式, RST

  // Other names for the same wires on the sheet: Cout = \进位_借位 ; Din[15:0] = \预置数据 ; SDin[7:0] = \预置数据 [7:0];
  //   MDin[7:0] = \预置数据 [15:8]; En = \使能 ; Min[7:0] = Minute; Mode = \计数模式 ; PreSet = \异步置位 ; Sec[7:0] = Second

  // Notes on the sheet:
  //   请勿增删改引脚，否则可能导致电路封装变化，无法测试！！！
  //   正计数到59：59，倒计数到0时输出为1
endmodule

module \厨房计时器状态机  (
  input  S2,
  input  S1,
  input  S0,
  input  mode,
  input  start,
  input  timer,
  input  finished,
  output N2,
  output N1,
  output N0
);
endmodule

module \厨房计时器输出函数  (
  input  S2,
  input  S1,
  input  S0,
  output Preset,
  output CounterEn,
  output AlertTimerEnable,
  output Runing
);
endmodule

module \厨房计数器  (
);

  wire _0_5HZ, _1HZ, _16HZ, Alert, undriven, \分 , \开始_暂停 , \归零 , \时间到 , \秒 ;
  wire [0:0] counter_1_q;
  wire [2:0] S1B, S2B, S3B, S4B;
  wire [3:0] S1T, S2T, S3T, S4T;

  _7_Segment_Display #(.active("true")) u_7_segment_display_1 (
    .g(S4T[0]), .f(S4T[1]), .a(S4T[2]), .b(S4T[3]), .e(S4B[0]), .d(S4B[1]), .c(S4B[2]));  // open: dp
  _7_Segment_Display #(.active("true")) u_7_segment_display_2 (
    .g(S2T[0]), .f(S2T[1]), .a(S2T[2]), .b(S2T[3]), .e(S2B[0]), .d(S2B[1]), .c(S2B[2]));  // open: dp
  _7_Segment_Display #(.active("true")) u_7_segment_display_3 (
    .g(S3T[0]), .f(S3T[1]), .a(S3T[2]), .b(S3T[3]), .e(S3B[0]), .d(S3B[1]), .c(S3B[2]));  // open: dp
  Button button_1 (.out(\分 ));
  _7_Segment_Display #(.active("true")) u_7_segment_display_4 (
    .g(S1T[0]), .f(S1T[1]), .a(S1T[2]), .b(S1T[3]), .e(S1B[0]), .d(S1B[1]), .c(S1B[2]));  // open: dp
  Button button_2 (.out(\开始_暂停 ));
  Button button_3 (.out(\秒 ));
  Button button_4 (.out(\归零 ));
  Clock #(.highDuration(1), .lowDuration(1)) clock_1 (.out(_16HZ));
  Counter #(.width(3), .max('h7), .ongoal("wrap"), .trigger("rising"), .behavior("new")) counter_1 (
    .count(undriven), .Q({_1HZ, _0_5HZ, counter_1_q[0]}), .clk(_16HZ), .preset(undriven));  // open: load, D, carry, clr, down
  and and_1 (\时间到 , Alert, _1HZ);
  // Buzzer #(.freq_measure("Hz"), .vol_width(7)) buzzer_1: pin names not known; wires that end beside it: 14'h1000, \时间到 , {7{1'b1}}

  // Notes on the sheet:
  //   厨房计时器
  //   分频电路
  //   蜂鸣器
endmodule
